// Logisim project Questao03Circuito.circ as structural Verilog: 1 circuit, main circuit main
module main (
  input  A
);

  wire clock_1_out, d_ff_1_q, d_ff_1_qn, multiplexer_1_out;

  Clock clock_1 (.out(clock_1_out));
  D_Flip_Flop d_ff_1 (.clk(clock_1_out), .D(multiplexer_1_out), .Q(d_ff_1_q), .Qn(d_ff_1_qn));  // open: preset, reset
  Multiplexer #(.enable("false")) multiplexer_1 (.in0(d_ff_1_q), .in1(d_ff_1_qn), .out(multiplexer_1_out), .sel(A));
endmodule
