// Logisim project Questao05.circ as structural Verilog: 1 circuit, main circuit main
module main (
  output out_1,
  output out_2
);

  wire A_qn, clock_1_out;

  Clock clock_1 (.out(clock_1_out));
  D_Flip_Flop B (.clk(clock_1_out), .D(A_qn), .Q(out_2));  // open: Qn, preset, reset
  D_Flip_Flop A (.clk(clock_1_out), .D(out_2), .Q(out_1), .Qn(A_qn));  // open: preset, reset
endmodule
