// Logisim project Questao08.circ as structural Verilog: 1 circuit, main circuit main
module main (
  input  in_1,
  output A,
  output B,
  output C,
  output D,
  output E
);

  wire clock_1_out;

  Clock clock_1 (.out(clock_1_out));
  J_K_Flip_Flop j_k_ff_1 (.J(in_1), .clk(clock_1_out), .K(in_1), .Q(A));  // open: Qn, preset, reset
  J_K_Flip_Flop j_k_ff_2 (.J(A), .clk(A), .K(A), .Q(B));  // open: Qn, preset, reset
  J_K_Flip_Flop j_k_ff_3 (.J(B), .clk(B), .K(B), .Q(C));  // open: Qn, preset, reset
  J_K_Flip_Flop j_k_ff_4 (.J(C), .clk(C), .K(C), .Q(D));  // open: Qn, preset, reset
  and and_1 (E, B, A, D, in_1, C);
endmodule
