// Logisim project Questao10.circ as structural Verilog: 1 circuit, main circuit main
module main (
  input  in_1,
  output out_2,
  output out_3,
  output out_4,
  output out_5
);

  wire clock_1_out;

  Clock clock_1 (.out(clock_1_out));
  T_Flip_Flop D (.clk(clock_1_out), .T(in_1), .Qn(out_2));  // open: Q, preset, reset
  T_Flip_Flop C (.clk(out_2), .T(out_2), .Qn(out_3));  // open: Q, preset, reset
  T_Flip_Flop B (.clk(out_3), .T(out_3), .Qn(out_4));  // open: Q, preset, reset
  T_Flip_Flop A (.clk(out_4), .T(out_4), .Q(out_5));  // open: Qn, preset, reset
endmodule
