// Logisim project Questao02.circ as structural Verilog: 1 circuit, main circuit main
module main (
  input  Adress,
  input  Read_Write,
  input  in0,
  input  in_1,
  input  in_2,
  input  Clear,
  input  in_3,
  output out_8,
  output out_9,
  output out_10,
  output out_11
);

  wire and_1_out, and_2_out, and_3_out, and_4_out, clock_1_out, d_ff_1_q, d_ff_2_q, d_ff_3_q, d_ff_4_q;

  Clock clock_1 (.out(clock_1_out));
  and and_1 (and_1_out, Adress, Read_Write, clock_1_out);
  and and_2 (and_2_out, Adress, Read_Write, clock_1_out);
  and and_3 (and_3_out, Adress, Read_Write, clock_1_out);
  and and_4 (and_4_out, Adress, Read_Write, clock_1_out);
  D_Flip_Flop d_ff_1 (.clk(and_1_out), .D(in0), .Q(d_ff_1_q), .reset(Clear));  // open: Qn, preset
  and and_5 (out_8, Adress, d_ff_1_q);
  D_Flip_Flop d_ff_2 (.clk(and_2_out), .D(in_1), .Q(d_ff_2_q), .reset(Clear));  // open: Qn, preset
  D_Flip_Flop d_ff_3 (.clk(and_3_out), .D(in_2), .Q(d_ff_3_q), .reset(Clear));  // open: Qn, preset
  D_Flip_Flop d_ff_4 (.clk(and_4_out), .D(in_3), .Q(d_ff_4_q), .reset(Clear));  // open: Qn, preset
  and and_6 (out_11, d_ff_4_q, Adress);
  and and_7 (out_9, Adress, d_ff_2_q);
  and and_8 (out_10, d_ff_3_q, Adress);
endmodule
