// Logisim project Questão 01.circ as structural Verilog: 1 circuit, main circuit main
module main (
  input  in1,
  input  K,
  input  in0,
  input  Adress,
  input  K_2,
  input  Clear,
  output Output1,
  output Output0
);

  wire and_1_out, and_2_out, Clock_out, j_k_ff_1_q, j_k_ff_2_q;

  Clock Clock (.out(Clock_out));
  and and_1 (and_1_out, Adress, Clock_out);
  and and_2 (and_2_out, Adress, Clock_out);
  J_K_Flip_Flop j_k_ff_1 (.J(in0), .clk(and_1_out), .K(K_2), .Q(j_k_ff_1_q), .reset(Clear));  // open: Qn, preset, en
  J_K_Flip_Flop j_k_ff_2 (.J(in1), .clk(and_2_out), .K(K), .Q(j_k_ff_2_q), .reset(Clear));  // open: Qn, preset, en
  and and_3 (Output0, Adress, j_k_ff_1_q);
  and and_4 (Output1, j_k_ff_2_q, Adress);
endmodule
