// Logisim project Questao02.circ as structural Verilog: 1 circuit, main circuit main
module main (
  input  Clear,
  input  Input,
  output _2_4,
  output _2_3,
  output _2_3_2,
  output _2_2,
  output _2_1
);

  wire Clock_out, j_k_ff_2_q, j_k_ff_3_q, j_k_ff_4_q, j_k_ff_5_q;

  Clock Clock (.out(Clock_out));
  J_K_Flip_Flop j_k_ff_1 (.J(Input), .clk(j_k_ff_2_q), .K(Input), .Qn(_2_4), .preset(Clear));  // open: Q, reset
  J_K_Flip_Flop j_k_ff_2 (
    .J(Input), .clk(j_k_ff_3_q), .K(Input), .Q(j_k_ff_2_q), .Qn(_2_3), .preset(Clear));  // open: reset
  J_K_Flip_Flop j_k_ff_3 (
    .J(Input), .clk(j_k_ff_4_q), .K(Input), .Q(j_k_ff_3_q), .Qn(_2_3_2), .preset(Clear));  // open: reset
  J_K_Flip_Flop j_k_ff_4 (
    .J(Input), .clk(j_k_ff_5_q), .K(Input), .Q(j_k_ff_4_q), .Qn(_2_2), .preset(Clear));  // open: reset
  J_K_Flip_Flop j_k_ff_5 (
    .J(Input), .clk(Clock_out), .K(Input), .Q(j_k_ff_5_q), .Qn(_2_1), .preset(Clear));  // open: reset

  // Notes on the sheet:
  //   Gustavo Martins Lopes da Costa 690773
  //   Contador crescente de 5 bits 
endmodule
