// Logisim project Questão01.circ as structural Verilog
module main (
  input  Clear,
  input  Input,
  output _2_4,
  output _2_3,
  output _2_2,
  output _2_1,
  output _2_0
);

  wire clock_out;

  Clock clock (.out(clock_out));
  J_K_Flip_Flop j_k_ff_1 (.J(Input), .clk(_2_3), .K(Input), .Qn(_2_4), .preset(Clear));  // open: Q, reset
  J_K_Flip_Flop j_k_ff_2 (.J(Input), .clk(_2_2), .K(Input), .Qn(_2_3), .preset(Clear));  // open: Q, reset
  J_K_Flip_Flop j_k_ff_3 (.J(Input), .clk(_2_1), .K(Input), .Qn(_2_2), .preset(Clear));  // open: Q, reset
  J_K_Flip_Flop j_k_ff_4 (.J(Input), .clk(_2_0), .K(Input), .Qn(_2_1));  // open: Q, preset, reset
  J_K_Flip_Flop j_k_ff_5 (.J(Input), .clk(clock_out), .K(Input), .Qn(_2_0), .preset(Clear));  // open: Q, reset

  // Notes on the sheet:
  //   Gustavo Martins Lopes da Costa 690773
  //   Contador Assíncrono decrescente de 5 bytes
endmodule
