// Logisim project Questão03.circ as structural Verilog: 1 circuit, main circuit main
module main (
  input  Clear,
  input  Input,
  output _2_3,
  output _2_2,
  output _2_1,
  output _2_0
);

  wire and_1_out, Clock_out, j_k_ff_1_qn, j_k_ff_2_qn, j_k_ff_3_qn, nand_1_out, not_1_out, not_2_out;

  Clock Clock (.out(Clock_out));
  nand nand_1 (nand_1_out, not_1_out, _2_1, not_2_out, _2_3);
  and and_1 (and_1_out, Clear, nand_1_out);
  not not_1 (not_1_out, _2_0);
  not not_2 (not_2_out, _2_2);
  J_K_Flip_Flop j_k_ff_1 (
    .J(Input), .clk(Clock_out), .K(Input), .Q(_2_0), .Qn(j_k_ff_1_qn), .reset(and_1_out));  // open: preset
  J_K_Flip_Flop j_k_ff_2 (
    .J(Input), .clk(j_k_ff_1_qn), .K(Input), .Q(_2_1), .Qn(j_k_ff_2_qn), .reset(and_1_out));  // open: preset
  J_K_Flip_Flop j_k_ff_3 (
    .J(Input), .clk(j_k_ff_2_qn), .K(Input), .Q(_2_2), .Qn(j_k_ff_3_qn), .reset(and_1_out));  // open: preset
  J_K_Flip_Flop j_k_ff_4 (.J(Input), .clk(j_k_ff_3_qn), .K(Input), .Q(_2_3), .reset(and_1_out));  // open: Qn, preset

  // Notes on the sheet:
  //   Gustavo Martins Lopes da Costa 690773
  //   Contador Decádico crescente de 4bits
endmodule
