// Logisim project Questão04.circ as structural Verilog: 1 circuit, main circuit main
module main (
  input  Clear,
  input  Input,
  output _2_3,
  output _2_2,
  output _2_1,
  output _2_0
);

  wire Clock_out, j_k_ff_1_qn, j_k_ff_2_qn, j_k_ff_3_qn, j_k_ff_4_qn, nand_1_out, not_1_out, not_2_out,
       not_3_out, or_1_out;

  Clock Clock (.out(Clock_out));
  nand nand_1 (nand_1_out, not_2_out, j_k_ff_2_qn, not_3_out, j_k_ff_4_qn);
  or or_1 (or_1_out, nand_1_out, not_1_out);
  not not_1 (not_1_out, Input);
  not not_2 (not_2_out, j_k_ff_1_qn);
  not not_3 (not_3_out, j_k_ff_3_qn);
  J_K_Flip_Flop j_k_ff_1 (
    .J(Input), .clk(Clock_out), .K(Input), .Q(_2_0), .Qn(j_k_ff_1_qn), .reset(Clear));  // open: preset
  J_K_Flip_Flop j_k_ff_2 (
    .J(or_1_out), .clk(_2_0), .K(or_1_out), .Q(_2_1), .Qn(j_k_ff_2_qn), .reset(Clear));  // open: preset
  J_K_Flip_Flop j_k_ff_3 (
    .J(or_1_out), .clk(_2_1), .K(or_1_out), .Q(_2_2), .Qn(j_k_ff_3_qn), .reset(Clear));  // open: preset
  J_K_Flip_Flop j_k_ff_4 (
    .J(or_1_out), .clk(_2_2), .K(or_1_out), .Q(_2_3), .Qn(j_k_ff_4_qn), .reset(Clear));  // open: preset

  // Notes on the sheet:
  //   Contador Decádico Decrescente de 4bits
endmodule
