// Logisim project Questão05.circ as structural Verilog: 1 circuit, main circuit main
module main (
  input  Input,
  input  Clear,
  output out_3,
  output out_4,
  output out_5,
  output out_6,
  output out_7,
  output out_8,
  output out_9,
  output out_10
);

  wire and_1_out, and_2_out, and_3_out, and_4_out, and_5_out, Clock_out;

  Clock Clock (.out(Clock_out));
  T_Flip_Flop t_ff_1 (.clk(Clock_out), .T(Input), .Q(out_3), .reset(Clear));  // open: Qn, preset
  T_Flip_Flop t_ff_2 (.clk(Clock_out), .T(and_4_out), .Q(out_7), .reset(Clear));  // open: Qn, preset
  T_Flip_Flop t_ff_3 (.clk(Clock_out), .T(out_3), .Q(out_4), .reset(Clear));  // open: Qn, preset
  T_Flip_Flop t_ff_4 (.clk(Clock_out), .T(out_7), .Q(out_8), .reset(Clear));  // open: Qn, preset
  T_Flip_Flop t_ff_5 (.clk(Clock_out), .T(and_1_out), .Q(out_5), .reset(Clear));  // open: Qn, preset
  and and_1 (and_1_out, out_4, out_3);
  and and_2 (and_2_out, out_5, out_4, out_3);
  T_Flip_Flop t_ff_6 (.clk(Clock_out), .T(and_3_out), .Q(out_9), .preset(out_8), .reset(Clear));  // open: Qn
  and and_3 (and_3_out, out_7, out_8);
  T_Flip_Flop t_ff_7 (.clk(Clock_out), .T(and_2_out), .Q(out_6), .reset(Clear));  // open: Qn, preset
  and and_4 (and_4_out, and_2_out, out_6);
  T_Flip_Flop t_ff_8 (.clk(Clock_out), .T(and_5_out), .Q(out_10), .preset(out_8), .reset(Clear));  // open: Qn
  and and_5 (and_5_out, out_7, out_9, out_8);

  // Notes on the sheet:
  //   Gustavo Martins Lopes da Costa 690773
  //   Contador  síncrono de 8 bits  
endmodule
