// Logisim project Questão06.circ as structural Verilog: 1 circuit, main circuit main
module main (
  input  Input,
  input  Clear,
  output out_3,
  output out_4,
  output out_5,
  output out_6,
  output out_7,
  output out_8
);

  wire Clock_out, j_k_ff_3_qn, not_1_out, not_2_out, not_3_out, not_4_out, not_5_out, not_6_out, or_1_out;

  Clock Clock (.out(Clock_out));
  or or_1 (or_1_out, out_8, Input);
  J_K_Flip_Flop j_k_ff_1 (.J(or_1_out), .clk(Clock_out), .K(not_1_out), .Q(out_3), .reset(Clear));  // open: Qn, preset
  not not_1 (not_1_out, or_1_out);
  not not_2 (not_2_out, out_3);
  J_K_Flip_Flop j_k_ff_2 (.J(out_3), .clk(Clock_out), .K(not_2_out), .Q(out_4), .reset(Clear));  // open: Qn, preset
  J_K_Flip_Flop j_k_ff_3 (
    .J(out_4), .clk(Clock_out), .K(not_3_out), .Q(out_5), .Qn(j_k_ff_3_qn), .reset(Clear));  // open: preset
  not not_3 (not_3_out, out_4);
  not not_4 (not_4_out, out_5);
  J_K_Flip_Flop j_k_ff_4 (.J(out_5), .clk(Clock_out), .K(not_4_out), .Q(out_6), .reset(Clear));  // open: Qn, preset
  not not_5 (not_5_out, out_6);
  J_K_Flip_Flop j_k_ff_5 (.J(out_6), .clk(Clock_out), .K(not_5_out), .Q(out_7), .reset(Clear));  // open: Qn, preset
  not not_6 (not_6_out, out_7);
  J_K_Flip_Flop j_k_ff_6 (.J(out_7), .clk(Clock_out), .K(not_6_out), .Q(out_8), .reset(Clear));  // open: Qn, preset

  // Notes on the sheet:
  //   Gustavo Martins lopes da Costa 690773
  //   Ring counter de 6 bits
endmodule
