// Logisim project Questao01.circ as structural Verilog: 1 circuit, main circuit main
module main (
  input  Clear,
  input  Load,
  output Bit_1,
  output Bit_2,
  output Bit_3,
  output Bit_4,
  output Bit_5,
  output Bit_6
);

  wire Clock_out;

  Clock Clock (.out(Clock_out));
  D_Flip_Flop d_ff_1 (.clk(Clock_out), .D(Bit_2), .Q(Bit_1), .reset(Clear));  // open: Qn, preset
  D_Flip_Flop d_ff_2 (.clk(Clock_out), .D(Bit_3), .Q(Bit_2), .reset(Clear));  // open: Qn, preset
  D_Flip_Flop d_ff_3 (.clk(Clock_out), .D(Bit_4), .Q(Bit_3), .reset(Clear));  // open: Qn, preset
  D_Flip_Flop d_ff_4 (.clk(Clock_out), .D(Bit_5), .Q(Bit_4), .reset(Clear));  // open: Qn, preset
  D_Flip_Flop d_ff_5 (.clk(Clock_out), .D(Bit_6), .Q(Bit_5), .reset(Clear));  // open: Qn, preset
  D_Flip_Flop d_ff_6 (.clk(Clock_out), .D(Load), .Q(Bit_6), .reset(Clear));  // open: Qn, preset
endmodule
