// Logisim project Questao02.circ as structural Verilog: 1 circuit, main circuit main
module main (
  input  in_1,
  input  in_2,
  input  in_3,
  input  Entrada,
  input  in_5,
  input  in_6,
  output out_7,
  output out_8,
  output out_9,
  output out_10,
  output out_11,
  output out_12
);

  wire and_1_out, and_2_out, and_3_out, and_4_out, and_5_out, Clock_out;

  Clock Clock (.out(Clock_out));
  and and_1 (and_1_out, Entrada, in_2);
  and and_2 (and_2_out, Entrada, in_6);
  D_Flip_Flop d_ff_1 (.clk(Clock_out), .D(out_8), .Q(out_7), .preset(and_1_out));  // open: Qn, reset
  D_Flip_Flop #(.Pre_Clr_Positions("LEGACY")) d_ff_2 (
    .clk(Clock_out), .D(out_12), .Q(out_11), .preset(and_2_out));  // open: Qn, reset
  and and_3 (and_3_out, Entrada, in_1);
  D_Flip_Flop #(.Pre_Clr_Positions("LEGACY")) d_ff_3 (
    .clk(Clock_out), .D(out_10), .Q(out_12), .preset(and_4_out));  // open: Qn, reset
  and and_4 (and_4_out, Entrada, in_5);
  D_Flip_Flop d_ff_4 (.clk(Clock_out), .D(out_9), .Q(out_8), .preset(and_3_out));  // open: Qn, reset
  and and_5 (and_5_out, Entrada, in_3);
  D_Flip_Flop d_ff_5 (.clk(Clock_out), .D(Entrada), .Q(out_10));  // open: Qn, preset, reset
  D_Flip_Flop d_ff_6 (.clk(Clock_out), .D(out_11), .Q(out_9), .preset(and_5_out));  // open: Qn, reset

  // Notes on the sheet:
  //   Deslocador para a esquerda com carga inicial em todos os estágios
endmodule
