// Logisim project Questao03.circ as structural Verilog: 1 circuit, main circuit main
module main (
  input  Clear,
  output out_2,
  output out_3,
  output out_4,
  output out_5,
  output out_6,
  output out_7
);

  wire clock_out;

  Clock clock (.out(clock_out));
  D_Flip_Flop #(.Pre_Clr_Positions("LEGACY")) d_ff_1 (
    .clk(clock_out), .D(out_2), .Q(out_7), .preset(Clear));  // open: Qn, reset
  D_Flip_Flop d_ff_2 (.clk(clock_out), .D(out_7), .Q(out_6), .reset(Clear));  // open: Qn, preset
  D_Flip_Flop d_ff_3 (.clk(clock_out), .D(out_6), .Q(out_5), .reset(Clear));  // open: Qn, preset
  D_Flip_Flop d_ff_4 (.clk(clock_out), .D(out_5), .Q(out_4), .reset(Clear));  // open: Qn, preset
  D_Flip_Flop d_ff_5 (.clk(clock_out), .D(out_4), .Q(out_3), .reset(Clear));  // open: Qn, preset
  D_Flip_Flop d_ff_6 (.clk(clock_out), .D(out_3), .Q(out_2), .reset(Clear));  // open: Qn, preset
endmodule
