// Logisim project Questao04.circ as structural Verilog: 1 circuit, main circuit main
module main (
  input  clear,
  input  Input,
  output out_3,
  output out_4,
  output out_5,
  output out_6,
  output out_7,
  output out_8
);

  wire clock_out, or_1_out;

  Clock clock (.out(clock_out));
  or or_1 (or_1_out, out_8, Input);
  D_Flip_Flop d_ff_1 (.clk(clock_out), .D(out_7), .Q(out_8), .reset(clear));  // open: Qn, preset
  D_Flip_Flop d_ff_2 (.clk(clock_out), .D(out_6), .Q(out_7), .reset(clear));  // open: Qn, preset
  D_Flip_Flop d_ff_3 (.clk(clock_out), .D(out_5), .Q(out_6), .reset(clear));  // open: Qn, preset
  D_Flip_Flop d_ff_4 (.clk(clock_out), .D(out_4), .Q(out_5), .reset(clear));  // open: Qn, preset
  D_Flip_Flop d_ff_5 (.clk(clock_out), .D(out_3), .Q(out_4));  // open: Qn, preset, reset
  D_Flip_Flop d_ff_6 (.clk(clock_out), .D(or_1_out), .Q(out_3));  // open: Qn, preset, reset

  // Notes on the sheet:
  //   Twisted ring para a esquerda
endmodule
