// Logisim project Questao05.circ as structural Verilog: 1 circuit, main circuit main
module main (
  input  clear,
  input  in_2,
  input  in_3,
  input  in_4,
  input  in_5,
  input  in_6,
  output out_7,
  output out_8,
  output out_9,
  output out_10
);

  wire and_1_out, and_2_out, and_3_out, and_4_out, clock_1_out;

  Clock clock_1 (.out(clock_1_out));
  and and_1 (and_1_out, in_2, in_3);
  D_Flip_Flop #(.enable("true")) d_ff_1 (
    .clk(clock_1_out), .D(1'b1), .Q(out_7), .en(and_1_out), .reset(clear));  // open: Qn, preset
  and and_2 (and_2_out, in_2, in_4);
  D_Flip_Flop #(.enable("true")) d_ff_2 (
    .clk(clock_1_out), .D(out_7), .Q(out_8), .en(and_2_out), .reset(clear));  // open: Qn, preset
  and and_3 (and_3_out, in_2, in_5);
  D_Flip_Flop #(.enable("true")) d_ff_3 (
    .clk(clock_1_out), .D(out_8), .Q(out_9), .en(and_3_out), .reset(clear));  // open: Qn, preset
  and and_4 (and_4_out, in_2, in_6);
  D_Flip_Flop #(.enable("true")) d_ff_4 (
    .clk(clock_1_out), .D(out_9), .Q(out_10), .en(and_4_out), .reset(clear));  // open: Qn, preset
endmodule
