// Logisim project Questao06.circ as structural Verilog: 1 circuit, main circuit main
module main (
  input  Clear,
  input  in_2,
  input  in_3,
  input  in_4,
  input  in_5,
  input  in_6,
  output out_7,
  output out_8,
  output out_9,
  output out_10,
  output out_11,
  output out_12
);

  wire Clock_out, demultiplexer_1_out0, demultiplexer_1_out1, demultiplexer_2_out0, demultiplexer_2_out1,
       demultiplexer_3_out0, demultiplexer_3_out1, demultiplexer_4_out0, demultiplexer_4_out1,
       demultiplexer_5_out0, demultiplexer_5_out1;

  Clock Clock (.out(Clock_out));
  D_Flip_Flop #(.Pre_Clr_Positions("LEGACY")) d_ff_1 (
    .clk(Clock_out), .D(out_8), .Q(out_11), .preset(demultiplexer_1_out1), .reset(demultiplexer_1_out0));  // open: Qn
  Demultiplexer #(.enable("false")) demultiplexer_1 (
    .out0(demultiplexer_1_out0), .out1(demultiplexer_1_out1), .in(Clear), .sel(in_2));
  D_Flip_Flop #(.Pre_Clr_Positions("LEGACY")) d_ff_2 (
    .clk(Clock_out), .D(out_10), .Q(out_8), .preset(demultiplexer_2_out1), .reset(demultiplexer_2_out0));  // open: Qn
  Demultiplexer #(.enable("false")) demultiplexer_2 (
    .out0(demultiplexer_2_out0), .out1(demultiplexer_2_out1), .in(Clear), .sel(in_3));
  D_Flip_Flop #(.Pre_Clr_Positions("LEGACY")) d_ff_3 (
    .clk(Clock_out), .D(out_7), .Q(out_10), .preset(demultiplexer_3_out1), .reset(demultiplexer_3_out0));  // open: Qn
  Demultiplexer #(.enable("false")) demultiplexer_3 (
    .out0(demultiplexer_3_out0), .out1(demultiplexer_3_out1), .in(Clear), .sel(in_4));
  D_Flip_Flop #(.Pre_Clr_Positions("LEGACY")) d_ff_4 (
    .clk(Clock_out), .D(out_12), .Q(out_7), .preset(demultiplexer_4_out1), .reset(demultiplexer_4_out0));  // open: Qn
  Demultiplexer #(.enable("false")) demultiplexer_4 (
    .out0(demultiplexer_4_out0), .out1(demultiplexer_4_out1), .in(Clear), .sel(in_5));
  D_Flip_Flop #(.Pre_Clr_Positions("LEGACY")) d_ff_5 (
    .clk(Clock_out), .D(out_9), .Q(out_12), .preset(demultiplexer_5_out1), .reset(demultiplexer_5_out0));  // open: Qn
  Demultiplexer #(.enable("false")) demultiplexer_5 (
    .out0(demultiplexer_5_out0), .out1(demultiplexer_5_out1), .in(Clear), .sel(in_6));
  D_Flip_Flop #(.Pre_Clr_Positions("LEGACY")) d_ff_6 (
    .clk(Clock_out), .D(out_11), .Q(out_9), .preset(Clear));  // open: Qn, reset

  // Notes on the sheet:
  //   Ring Counter com carga inicial escolhível em todas as etapas
endmodule
