// Logisim project Questao07.circ as structural Verilog: 1 circuit, main circuit main
module main (
  input  Entrada,
  input  Clear,
  input  in_3,
  input  in_4,
  input  in_5,
  input  in_6,
  input  in_7,
  output out_8,
  output out_9,
  output out_10,
  output out_11,
  output out_12,
  output out_13
);

  wire and_1_out, and_2_out, and_3_out, and_4_out, and_5_out, Clock_out, or_1_out;

  Clock Clock (.out(Clock_out));
  or or_1 (or_1_out, Entrada, out_8);
  D_Flip_Flop d_ff_1 (.clk(Clock_out), .D(or_1_out), .Q(out_13), .reset(Clear));  // open: Qn, preset
  and and_1 (and_1_out, Entrada, in_3);
  D_Flip_Flop #(.Pre_Clr_Positions("LEGACY")) d_ff_2 (
    .clk(Clock_out), .D(out_13), .Q(out_12), .preset(and_1_out), .reset(Clear));  // open: Qn
  D_Flip_Flop #(.Pre_Clr_Positions("LEGACY")) d_ff_3 (
    .clk(Clock_out), .D(out_12), .Q(out_11), .preset(and_2_out), .reset(Clear));  // open: Qn
  and and_2 (and_2_out, Entrada, in_4);
  and and_3 (and_3_out, Entrada, in_5);
  D_Flip_Flop #(.Pre_Clr_Positions("LEGACY")) d_ff_4 (
    .clk(Clock_out), .D(out_11), .Q(out_10), .preset(and_3_out), .reset(Clear));  // open: Qn
  D_Flip_Flop #(.Pre_Clr_Positions("LEGACY")) d_ff_5 (
    .clk(Clock_out), .D(out_10), .Q(out_9), .preset(and_4_out), .reset(Clear));  // open: Qn
  and and_4 (and_4_out, Entrada, in_6);
  and and_5 (and_5_out, Entrada, in_7);
  D_Flip_Flop #(.Pre_Clr_Positions("LEGACY")) d_ff_6 (
    .clk(Clock_out), .D(out_9), .Q(out_8), .preset(and_5_out), .reset(Clear));  // open: Qn

  // Notes on the sheet:
  //   Ring Counter para a direita com 6 bist e carga inicial em todos os estágios
endmodule
