// Logisim project ProjetoQuestao03.circ as structural Verilog: 1 circuit, main circuit main
module main (
  input  A,
  input  B,
  input  Chave_And___Nand,
  input  A_2,
  input  B_2,
  input  \Seleção_por_grupo ,
  input  Chave_Or_Nor,
  output out_8
);

  wire and_1_out, nand_1_out, nand_2_out, nand_3_out, nand_4_out, nand_5_out, nor_1_out, nor_2_out,
       nor_3_out, or_1_out;

  and and_1 (and_1_out, A, Chave_And___Nand);
  nand nand_1 (nand_1_out, B, Chave_And___Nand);
  nor nor_1 (nor_1_out, A_2, Chave_Or_Nor);
  or or_1 (or_1_out, Chave_Or_Nor, B_2);
  nand nand_2 (nand_2_out, and_1_out, nand_1_out);
  nor nor_2 (nor_2_out, nor_1_out, or_1_out);
  nor nor_3 (nor_3_out, nor_1_out, nor_2_out);
  nand nand_3 (nand_3_out, nand_2_out, nand_2_out);
  nand nand_4 (nand_4_out, nand_3_out, \Seleção_por_grupo );
  nand nand_5 (nand_5_out, nor_3_out, \Seleção_por_grupo );
  nand nand_6 (out_8, nand_4_out, nand_5_out);
endmodule
