// Logisim project Projetos em logism.circ as structural Verilog: 1 circuit, main circuit main
module main (
  input  A,
  input  B,
  input  in_3,
  input  A_2,
  input  B_2,
  input  Chave,
  output out_7,
  output out_8
);

  wire and_1_out, nand_1_out, nand_2_out, nor_1_out, nor_2_out, or_1_out;

  and and_1 (and_1_out, A, in_3);
  nor nor_1 (nor_1_out, A_2, Chave);
  or or_1 (or_1_out, Chave, B_2);
  nand nand_1 (nand_1_out, B, in_3);
  nand nand_2 (nand_2_out, and_1_out, nand_1_out);
  nor nor_2 (nor_2_out, nor_1_out, or_1_out);
  nand nand_3 (out_7, nand_2_out, nand_2_out);
  nor nor_3 (out_8, nor_1_out, nor_2_out);

  // Notes on the sheet:
  //   Questão 01
  //   Questão 02
  //   MUX-Multiplexador com operações or e nor
  //   MUX-Multiplexador apenas com operações AND e NAND e duas saídas
  //   Guia 07
endmodule
