// Logisim project Aula16do10.circ as structural Verilog: 2 circuits, main circuit main
module main (
  input  in_1,
  input  in_2,
  input  in_3,
  input  in_4,
  input  in_5,
  input  in_6,
  input  in_7,
  input  in_8,
  input  in_9,
  input  in_10,
  input  in_11,
  output out_12,
  output out_13,
  output out_14,
  output out_15,
  output out_16,
  output out_17,
  output out_18,
  output out_19,
  output out_20,
  output out_21,
  output out_22,
  output out_23,
  output out_24,
  output out_25
);

  wire and_1_out, not_1_out, not_2_out, not_7_out, not_12_out, or_1_out, or_5_out, or_6_out;

  not not_1 (not_1_out, in_4);
  not not_2 (not_2_out, in_5);
  not not_3 (out_18, not_2_out);
  or or_1 (or_1_out, in_9, out_25);
  not not_4 (out_15, not_1_out);
  not not_5 (out_23, or_1_out);
  not not_6 (out_25, out_23);
  not not_7 (not_7_out, in_11);
  or or_2 (out_22, in_8, and_1_out);
  and and_1 (and_1_out, out_22, not_7_out);
  or or_3 (out_12, in_1, out_12);
  or or_4 (out_20, in_6, out_21);
  not not_8 (out_21, out_20);
  not not_9 (out_13, out_17);
  or or_5 (or_5_out, in_2, out_13);
  not not_10 (out_17, or_5_out);
  and and_2 (out_19, in_10, not_12_out);
  or or_6 (or_6_out, in_7, out_19);
  not not_11 (out_24, or_6_out);
  not not_12 (not_12_out, out_24);

  assign out_14 = in_3;
  assign out_16 = out_12;

  // Notes on the sheet:
  //   Aula 16/10
  //   Armazenando informação
  //   Metáfora do papa léguas
endmodule

module Guia_05 (
  input  in_1,
  input  A,
  input  B,
  input  in_4,
  input  in_5,
  input  in_6,
  input  A_2,
  input  in_8,
  input  B_2,
  input  in_10,
  input  in_11,
  input  in_12,
  output out_13,
  output out_14,
  output out_15,
  output out_16,
  output out_17,
  output out_18
);

  wire nand_1_out, nand_3_out, nand_4_out, nand_5_out, nand_6_out, nand_8_out, nand_9_out, nor_1_out,
       nor_2_out, nor_3_out, nor_6_out, nor_7_out, nor_8_out, nor_9_out;

  nand nand_1 (nand_1_out, in_5, in_6);
  nor nor_1 (nor_1_out, in_8, in_8);
  nor nor_2 (nor_2_out, in_10, in_10);
  nor nor_3 (nor_3_out, A, A, B, B);
  nor nor_4 (out_14, nor_3_out, nor_3_out);
  nand nand_2 (out_15, nand_1_out, nand_1_out);
  nor nor_5 (out_17, nor_1_out, nor_2_out);
  nand nand_3 (nand_3_out, in_1, in_1, in_1);
  nand nand_4 (nand_4_out, in_4, in_4, in_4);
  nor nor_6 (nor_6_out, A_2, A_2);
  nor nor_7 (nor_7_out, B_2, B_2);
  nand nand_5 (nand_5_out, in_11, in_11, in_11);
  nand nand_6 (nand_6_out, in_12, in_12);
  nand nand_7 (out_13, nand_3_out, nand_4_out);
  nor nor_8 (nor_8_out, nor_6_out, nor_7_out);
  nor nor_9 (nor_9_out, A_2, B_2);
  nand nand_8 (nand_8_out, nand_5_out, nand_6_out);
  nand nand_9 (nand_9_out, in_11, in_12);
  nor nor_10 (out_16, nor_8_out, nor_9_out);
  nand nand_10 (out_18, nand_8_out, nand_9_out);

  // Notes on the sheet:
  //   01.) Disjunção A | B utilizando apenas nor
  //   02.) Conjunção A & B utilizando apenas nand
  //   03.)Conjunção A & B apenas com nor
  //   04.)Disjunção A | B Apenas com NAND
  //   05 A xor B apenas com nor
  //   06.)A xnor B apenas com nand
endmodule
