// Logisim project Aula16do10part2.circ as structural Verilog: 1 circuit, main circuit main
module main (
  input  in_1,
  input  in_2,
  input  in_3,
  input  S,
  input  R,
  input  Enable,
  output out_7,
  output out_8,
  output Q,
  output Qnot
);

  wire not_1_out, s_r_ff_1_q, s_r_ff_1_qn;

  J_K_Flip_Flop j_k_ff_1 (.J(in_1), .clk(in_2), .K(in_2), .Q(out_7), .Qn(out_8));  // open: preset, en, reset
  S_R_Flip_Flop s_r_ff_1 (.S(S), .clk(Enable), .R(R), .Q(s_r_ff_1_q), .Qn(s_r_ff_1_qn));  // open: preset, reset, en
  not not_1 (not_1_out, Enable);
  S_R_Flip_Flop s_r_ff_2 (
    .S(s_r_ff_1_q), .clk(not_1_out), .R(s_r_ff_1_qn), .Q(Q), .Qn(Qnot));  // open: preset, reset, en

  assign in_3 = in_2;
endmodule
