// Logisim project FlipFlopJK com nand.circ as structural Verilog: 1 circuit, main circuit main
module main (
  input  J,
  input  K,
  output Q,
  output nQ
);

  wire clock_1_out, nand_1_out, nand_2_out;

  Clock clock_1 (.out(clock_1_out));
  nand nand_1 (nand_1_out, J, clock_1_out, nQ);
  nand nand_2 (nand_2_out, Q, clock_1_out, K);
  nand nand_3 (Q, nand_1_out, nQ);
  nand nand_4 (nQ, Q, nand_2_out);
endmodule
