// Logisim project Moore1011.circ as structural Verilog: 1 circuit, main circuit main
module main (
  input  Pulso,
  input  Clear,
  output out_3
);

  wire and_1_out, Clock_out, d_ff_1_q, d_ff_2_q, d_ff_3_q, d_ff_4_q, not_1_out, not_2_out;

  Clock Clock (.out(Clock_out));
  D_Flip_Flop d_ff_1 (.clk(Clock_out), .D(Pulso), .Q(d_ff_1_q), .reset(Clear));  // open: Qn, preset, en
  D_Flip_Flop d_ff_2 (.clk(Clock_out), .D(d_ff_1_q), .Q(d_ff_2_q), .reset(Clear));  // open: Qn, preset, en
  D_Flip_Flop d_ff_3 (.clk(Clock_out), .D(d_ff_2_q), .Q(d_ff_3_q), .reset(Clear));  // open: Qn, preset, en
  D_Flip_Flop d_ff_4 (.clk(Clock_out), .D(d_ff_3_q), .Q(d_ff_4_q), .reset(Clear));  // open: Qn, preset, en
  not not_1 (not_1_out, d_ff_2_q);
  not not_2 (not_2_out, Clock_out);
  D_Flip_Flop d_ff_5 (.clk(not_2_out), .D(and_1_out), .Q(out_3), .reset(Clear));  // open: Qn, preset, en
  and and_1 (and_1_out, d_ff_4_q, d_ff_3_q, not_1_out, d_ff_1_q);
endmodule
