// Logisim project Universalidade de Portas.circ as structural Verilog: 1 circuit, main circuit main
module main (
  input  A,
  input  in_2,
  input  A_2,
  input  in_4,
  input  B,
  input  in_6,
  input  A_3,
  input  in_8,
  input  B_2,
  input  in_10,
  output out_11,
  output out_12,
  output out_13,
  output out_14,
  output out_15,
  output out_16
);

  wire nand_2_out, nand_3_out, nand_4_out, nor_1_out, nor_2_out, nor_4_out;

  nand nand_1 (out_11, A, A);
  nand nand_2 (nand_2_out, A_2, B);
  nand nand_3 (nand_3_out, A_3, A_3);
  nand nand_4 (nand_4_out, B_2, B_2);
  nand nand_5 (out_13, nand_2_out, nand_2_out);
  nand nand_6 (out_15, nand_3_out, nand_4_out);
  nor nor_1 (nor_1_out, in_4, in_4);
  nor nor_2 (nor_2_out, in_6, in_6);
  not nor_3 (out_12, in_2);  // NOR_Gate
  nor nor_4 (nor_4_out, in_8, in_10);
  nor nor_5 (out_14, nor_1_out, nor_2_out);
  nor nor_6 (out_16, nor_4_out, nor_4_out);

  // Notes on the sheet:
  //   Not Utilizando apenas AND
  //   And utilizando duas NANDS
  //   Or utilizando três NANDS
  //   UNIVERSALIDADE DE PORTAS
  //   Or utilizando apenas NOR
  //   Not utilizando apenas NOR
  //   And utilizando apenas NOR
endmodule
