// Logisim project Xor.circ as structural Verilog: 1 circuit, main circuit main
module main (
  input  Input_A,
  input  Input_B,
  input  Input_A_2,
  input  Input_B_2,
  output Output,
  output Output_2
);

  wire not_1_out, not_2_out, or_1_out, or_2_out;

  not not_1 (not_1_out, Input_A);
  not not_2 (not_2_out, Input_B);
  xor xor_1 (Output_2, Input_A_2, Input_B_2);
  or or_1 (or_1_out, not_1_out, not_2_out);
  or or_2 (or_2_out, Input_A, Input_B);
  and and_1 (Output, or_1_out, or_2_out);

  // Notes on the sheet:
  //   Circuito de Xor apenas com or e ands
endmodule
