// Logisim project mux.circ as structural Verilog: 1 circuit, main circuit main
// chave
module main (
  input  in_1,
  input  in_2,
  input  A,
  input  in_4,
  input  in_5,
  input  B,
  input  in_7,
  input  in_8,
  input  Chave_de_selecao,
  input  A_2,
  input  B_2,
  input  in_12,
  output out_13,
  output \Saída ,
  output out_15
);

  wire and_1_out, and_2_out, and_3_out, multiplexer_1_out, multiplexer_2_out, nand_1_out;

  // NOT_Gate not_1 has open pins: in=Chave_de_selecao, out=open
  and and_1 (and_1_out, A_2, in_12);
  // NOT_Gate not_2 has open pins: in=in_12, out=open
  and and_2 (and_2_out, A, Chave_de_selecao);
  and and_3 (and_3_out, B, Chave_de_selecao);
  nand nand_1 (nand_1_out, B_2, in_12);
  and and_4 (out_15, and_1_out, nand_1_out);
  or or_1 (\Saída , and_2_out, and_3_out);
  Multiplexer multiplexer_1 (.in0(in_1), .in1(in_2), .out(multiplexer_1_out), .sel(in_7));  // open: en
  Multiplexer multiplexer_2 (.in0(in_4), .in1(in_5), .out(multiplexer_2_out), .sel(in_7));  // open: en
  Multiplexer multiplexer_3 (.in0(multiplexer_1_out), .in1(multiplexer_2_out), .out(out_13), .sel(in_8), .en(in_8));

  // Notes on the sheet:
  //   MUX-Multiplexador (Filtra)
  //   Multiplexador de 4 entradas
endmodule
