// Logisim project Contador Decádico.circ as structural Verilog: 1 circuit, main circuit main
module main (
  input  in_1,
  output out_2,
  output out_3,
  output out_4,
  output out_5
);

  wire clock_1_out, j_k_ff_1_qn, j_k_ff_2_qn, j_k_ff_4_qn, nand_1_out, undriven, undriven_2, undriven_3;

  Clock clock_1 (.out(clock_1_out));
  nand nand_1 (nand_1_out, j_k_ff_1_qn, j_k_ff_2_qn, out_5, j_k_ff_4_qn);
  J_K_Flip_Flop j_k_ff_1 (
    .J(in_1), .clk(out_4), .K(in_1), .Q(out_3), .Qn(j_k_ff_1_qn), .reset(undriven));  // open: preset
  J_K_Flip_Flop j_k_ff_2 (
    .J(in_1), .clk(out_5), .K(in_1), .Q(out_4), .Qn(j_k_ff_2_qn), .reset(undriven_2));  // open: preset
  J_K_Flip_Flop j_k_ff_3 (.J(in_1), .clk(out_2), .K(in_1), .Q(out_5), .reset(undriven_3));  // open: Qn, preset
  J_K_Flip_Flop j_k_ff_4 (.J(in_1), .clk(clock_1_out), .K(in_1), .Q(out_2), .Qn(j_k_ff_4_qn));  // open: preset, reset
endmodule
