// Logisim project Registradorde shift de quatro bits.circ as structural Verilog
module main (
  input  in_1,
  output out_2,
  output out_3,
  output out_4,
  output out_5
);

  wire clock_1_out;

  Clock clock_1 (.out(clock_1_out));
  D_Flip_Flop d_ff_1 (.clk(clock_1_out), .D(in_1), .Q(out_2));  // open: Qn, preset, reset
  D_Flip_Flop d_ff_2 (.clk(clock_1_out), .D(out_2), .Q(out_3));  // open: Qn, preset, reset
  D_Flip_Flop d_ff_3 (.clk(clock_1_out), .D(out_3), .Q(out_4));  // open: Qn, preset, reset
  D_Flip_Flop d_ff_4 (.clk(clock_1_out), .D(out_4), .Q(out_5));  // open: Qn, preset, reset
endmodule

module RS4bits_jk (
  input  in_1,
  output out_2,
  output out_3,
  output out_4,
  output out_5
);

  wire clock_1_out, j_k_ff_1_qn, j_k_ff_2_qn, j_k_ff_3_qn, not_1_out;

  Clock clock_1 (.out(clock_1_out));
  not not_1 (not_1_out, in_1);
  J_K_Flip_Flop j_k_ff_1 (
    .J(in_1), .clk(clock_1_out), .K(not_1_out), .Q(out_3), .Qn(j_k_ff_1_qn));  // open: preset, reset
  J_K_Flip_Flop j_k_ff_2 (
    .J(out_3), .clk(clock_1_out), .K(j_k_ff_1_qn), .Q(out_4), .Qn(j_k_ff_2_qn));  // open: preset, reset
  J_K_Flip_Flop j_k_ff_3 (
    .J(out_4), .clk(clock_1_out), .K(j_k_ff_2_qn), .Q(out_2), .Qn(j_k_ff_3_qn));  // open: preset, reset
  J_K_Flip_Flop j_k_ff_4 (.J(out_2), .clk(clock_1_out), .K(j_k_ff_3_qn), .Q(out_5));  // open: Qn, preset, reset

  // Notes on the sheet:
  //   Deslocador de 4 bits com Jks
endmodule

module Registrador_de_6_bits_a_esquerda (
  input  Clear,
  input  Load,
  output Bit_1,
  output Bit_2,
  output Bit_3,
  output Bit_4,
  output Bit_5,
  output Bit_6
);

  wire Clock_out;

  Clock Clock (.out(Clock_out));
  D_Flip_Flop d_ff_1 (.clk(Clock_out), .D(Bit_2), .Q(Bit_1), .reset(Clear));  // open: Qn, preset
  D_Flip_Flop d_ff_2 (.clk(Clock_out), .D(Bit_3), .Q(Bit_2), .reset(Clear));  // open: Qn, preset
  D_Flip_Flop d_ff_3 (.clk(Clock_out), .D(Bit_4), .Q(Bit_3), .reset(Clear));  // open: Qn, preset
  D_Flip_Flop d_ff_4 (.clk(Clock_out), .D(Bit_5), .Q(Bit_4), .reset(Clear));  // open: Qn, preset
  D_Flip_Flop d_ff_5 (.clk(Clock_out), .D(Bit_6), .Q(Bit_5), .reset(Clear));  // open: Qn, preset
  D_Flip_Flop d_ff_6 (.clk(Clock_out), .D(Load), .Q(Bit_6), .reset(Clear));  // open: Qn, preset
endmodule
