// Logisim project Regsitradores.circ as structural Verilog: 1 circuit, main circuit main
module main (
  input  [1:0] load,
  input  in_2,
  input  in_3,
  input  in_4,
  input  in_5,
  input  Load_2,
  output [1:0] out_7
);

  wire and_1_out, and_2_out, and_3_out, and_4_out, clock_1_out;

  Clock clock_1 (.out(clock_1_out));
  Register #(.width(2), .Select("low")) \Registrador_básico  (.D(load), .Q(out_7), .clk(clock_1_out));  // open: en, clr
  Clock clock_2 ();  // open: out
  and and_1 (and_1_out, Load_2, in_2);
  S_R_Flip_Flop s_r_ff_1 (.S(and_1_out));  // open: clk, R, Q, Qn, preset, reset
  and and_2 (and_2_out, Load_2, in_3);
  S_R_Flip_Flop s_r_ff_2 (.S(and_2_out));  // open: clk, R, Q, Qn, preset, reset
  and and_3 (and_3_out, Load_2, in_4);
  S_R_Flip_Flop s_r_ff_3 (.S(and_3_out));  // open: clk, R, Q, Qn, preset, reset
  and and_4 (and_4_out, Load_2, in_5);
  S_R_Flip_Flop s_r_ff_4 (.S(and_4_out));  // open: clk, R, Q, Qn, preset, reset

  // Notes on the sheet:
  //   Registradores
  //   Registrador paralelo-serie
endmodule
