// Logisim project Latch com nor.circ as structural Verilog: 1 circuit, main circuit main
module main (
  input  SET,
  input  RESET,
  output Q0,
  output Q
);

  nor nor_1 (Q0, SET, Q);
  nor nor_2 (Q, Q0, RESET);

  // Notes on the sheet:
  //   Latch com Nors
endmodule
