// Logisim project Latch sr com nands.circ as structural Verilog: 1 circuit, main circuit main
module main (
  input  Reset,
  input  Set,
  output Q0,
  output Q
);

  wire not_1_out, not_2_out;

  not not_1 (not_1_out, Set);
  not not_2 (not_2_out, Reset);
  nand nand_1 (Q0, not_2_out, Q);
  nand nand_2 (Q, Q0, not_1_out);

  // Notes on the sheet:
  //   Latch Sr com NANDs
endmodule
