// Logisim project Ram 1x1.circ as structural Verilog: 5 circuits, main circuit main
// 1x1
module main (
  input  Addr,
  input  R_W,
  input  Clock,
  input  Clear,
  input  entrada,
  output out_6
);

  wire and_1_out, d_ff_1_q;

  and and_1 (and_1_out, Addr, R_W, Clock);
  D_Flip_Flop d_ff_1 (.clk(and_1_out), .D(entrada), .Q(d_ff_1_q), .reset(Clear));  // open: Qn, preset
  and and_2 (out_6, Addr, d_ff_1_q);
endmodule

// 1x2
module Ram1x2 (
  input  Addr,
  input  R_W,
  input  Clock,
  input  in,
  input  Clear,
  output out_6
);

  wire demultiplexer_1_out0, demultiplexer_1_out1, main_1_out_6, main_2_out_6;

  Demultiplexer #(.enable("false")) demultiplexer_1 (
    .out0(demultiplexer_1_out0), .out1(demultiplexer_1_out1), .in(1'b1), .sel(Addr));
  main main_1 (
    .Addr(demultiplexer_1_out0), .R_W(R_W), .Clock(Clock), .entrada(in), .Clear(Clear), .out_6(main_1_out_6));
  main main_2 (
    .Addr(demultiplexer_1_out1), .R_W(R_W), .Clock(Clock), .entrada(in), .Clear(Clear), .out_6(main_2_out_6));
  Multiplexer #(.enable("false")) multiplexer_1 (.in0(main_1_out_6), .in1(main_2_out_6), .out(out_6), .sel(Addr));
endmodule

module _1x4 (
  input  Addr,
  input  R_W,
  input  in,
  input  Clear,
  output out_5,
  output out_6
);

  wire Clock_out, demultiplexer_1_out0, demultiplexer_1_out1, demultiplexer_2_out0, demultiplexer_2_out1,
       main_1_out_6, main_2_out_6, main_3_out_6, main_4_out_6;

  Demultiplexer #(.enable("false")) demultiplexer_1 (
    .out0(demultiplexer_1_out0), .out1(demultiplexer_1_out1), .in(1'b1), .sel(Addr));
  Demultiplexer #(.enable("false")) demultiplexer_2 (
    .out0(demultiplexer_2_out0), .out1(demultiplexer_2_out1), .in(1'b1), .sel(Addr));
  Clock Clock (.out(Clock_out));
  main main_1 (
    .Addr(demultiplexer_1_out0), .R_W(R_W), .Clock(Clock_out), .entrada(in), .Clear(Clear),
    .out_6(main_1_out_6));
  main main_2 (
    .Addr(demultiplexer_1_out1), .R_W(R_W), .Clock(Clock_out), .entrada(in), .Clear(Clear),
    .out_6(main_2_out_6));
  main main_3 (
    .Addr(demultiplexer_2_out0), .R_W(R_W), .Clock(Clock_out), .entrada(in), .Clear(Clear),
    .out_6(main_3_out_6));
  main main_4 (
    .Addr(demultiplexer_2_out1), .R_W(R_W), .Clock(Clock_out), .entrada(in), .Clear(Clear),
    .out_6(main_4_out_6));
  Multiplexer #(.enable("false")) multiplexer_1 (.in0(main_1_out_6), .in1(main_2_out_6), .out(out_5), .sel(Addr));
  Multiplexer #(.enable("false")) multiplexer_2 (.in0(main_3_out_6), .in1(main_4_out_6), .out(out_6), .sel(Addr));
endmodule

module _1x4com1x2 (
  input  \Memória_a_ser_salva ,
  input  R_W,
  input  Clear,
  input  [1:0] in_4,
  input  Bit_a_ser_salvo,
  output out_6
);

  wire Clock_out, demultiplexer_1_out0, demultiplexer_1_out1, multiplexer_1_out, ram1x2_1_out_6,
       ram1x2_2_out_6;

  Demultiplexer #(.enable("false")) demultiplexer_1 (
    .out0(demultiplexer_1_out0), .out1(demultiplexer_1_out1), .in(1'b1), .sel(\Memória_a_ser_salva ));
  Clock Clock (.out(Clock_out));
  Multiplexer #(.enable("false")) multiplexer_1 (
    .in0(in_4[0]), .in1(in_4[1]), .out(multiplexer_1_out), .sel(Bit_a_ser_salvo));
  Ram1x2 ram1x2_1 (
    .Addr(demultiplexer_1_out0), .R_W(R_W), .Clock(Clock_out), .in(multiplexer_1_out), .Clear(Clear),
    .out_6(ram1x2_1_out_6));
  Ram1x2 ram1x2_2 (
    .Addr(demultiplexer_1_out1), .R_W(R_W), .Clock(Clock_out), .in(multiplexer_1_out), .Clear(Clear),
    .out_6(ram1x2_2_out_6));
  Multiplexer #(.enable("false")) multiplexer_2 (
    .in0(ram1x2_1_out_6), .in1(ram1x2_2_out_6), .out(out_6), .sel(\Memória_a_ser_salva ));

  // Notes on the sheet:
  //   Imlementação de memória ram 1x4 utilizando 1x2
endmodule

// 1x2
module Ram1x2_2 (
  input  Addr,
  input  R_W,
  input  Clock,
  input  In0,
  input  In1,
  input  Clear,
  output out_7
);

  wire main_1_out_6, main_2_out_6;

  main main_1 (.Addr(Addr), .R_W(R_W), .Clock(Clock), .entrada(In0), .Clear(Clear), .out_6(main_1_out_6));
  main main_2 (.Addr(Addr), .R_W(R_W), .Clock(Clock), .entrada(In1), .Clear(Clear), .out_6(main_2_out_6));
  Multiplexer #(.enable("false")) multiplexer_1 (.in0(main_2_out_6), .in1(main_1_out_6), .out(out_7));  // open: sel
endmodule
