// Logisim project Memorizacao basia.circ as structural Verilog: 1 circuit, main circuit main
module main (
  input  in_1,
  output out_2
);

  or or_1 (out_2, out_2, in_1);

  // Notes on the sheet:
  //   Oh my god this is memory
endmodule
