// Logisim project latch D.circ as structural Verilog: 1 circuit, main circuit main
module main (
  input  D,
  output Q,
  output Q0
);

  wire clock_1_out, nand_1_out, nand_2_out, not_1_out;

  Clock clock_1 (.out(clock_1_out));
  not not_1 (not_1_out, D);
  D_Flip_Flop d_ff_1 ();  // open: clk, D, Q, Qn, preset, en, reset
  nand nand_1 (nand_1_out, D, clock_1_out);
  nand nand_2 (nand_2_out, clock_1_out, not_1_out);
  nand nand_3 (Q, nand_1_out, Q0);
  nand nand_4 (Q0, Q, nand_2_out);
endmodule
