// Logisim project memoria ram 1bit.circ as structural Verilog: 1 circuit, main circuit main
module main (
  input  R_W,
  input  adress,
  input  CLK,
  input  \input ,
  input  CLR,
  output \output 
);

  wire and_1_out, d_ff_1_q;

  and and_1 (and_1_out, adress, R_W, CLK);
  D_Flip_Flop d_ff_1 (.clk(and_1_out), .D(\input ), .Q(d_ff_1_q), .reset(CLR));  // open: Qn, preset, en
  and and_2 (\output , adress, d_ff_1_q);
endmodule
